# Fritzing sketch weather_station_v0.1 (saved by Fritzing 0.9.2b)
breadboards: 1

parts:
  ESP8266-1 = ESP8266-12 [part_number=ESP8266-12]
  DHT1 = DHT22 Humidity and Temperature Sensor
  Part1 = Adafruit_BMP280
  VCC1 = Battery
  S1 = Pushbutton [package="[SMD]"]
  LED1 = smd LED [color="Red (633nm)" package="0805 [SMD]"]
  LED2 = LED - 5mm [color="Red (633nm)" package="5 mm [THT]"]
  R1 = Resistor [tolerance=±0.05% resistance=330 package="0402 [SMD]"]
  R2 = Resistor [tolerance=±0.05% resistance=330 package="0402 [SMD]"]

nets:
  VCC: ESP8266-1.CH_PD, ESP8266-1.VCC, ESP8266-1.GPIO0, ESP8266-1.GPIO2, DHT1.VDD, Part1.3.3V, VCC1.+, S1.Pin_3, S1.Pin_4
  N1: ESP8266-1.GPIO14, LED1.cathode, R2.Pin_0
  N2: ESP8266-1.GPIO12, DHT1.DATA
  N3: ESP8266-1.GPIO13, LED2.cathode, R1.Pin_0
  N4: ESP8266-1.GPIO4, Part1.SDI/SDA
  N5: ESP8266-1.GPIO5, Part1.SCK/SCL
  GND: ESP8266-1.GPIO15, ESP8266-1.GND, DHT1.GND, Part1.GND, VCC1.-, R1.Pin_1, R2.Pin_1
  N6: S1.Pin_1, S1.Pin_2

custom parts:
  Adafruit_BMP280: Bosch has stepped up their game with their new BMP280 sensor, an environmental sensor with temperature, barometric pressure that is the next generation upgrade to the BMP085/BMP180/BMP183. This sensor is great for all sorts of weather sensing and can even be used in both I2C and SPI! This precision sensor from Bosch is the best low-cost, precision sensing solution for measuring barometric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
